# Fritzing sketch laser (saved by Fritzing 0.9.3b)
breadboards: 1

parts:
  Part1 = Arduino Uno (Rev3)
  Part2 = Adafruit VL6180X Time of Flight Distance Sensor [part_number="Adafruit #3316"]
  Part3 = Adafruit VL6180X Time of Flight Distance Sensor [part_number="Adafruit #3316"]

nets:
  N1: Part1.A4/SDA, Part2.SDA, Part3.SDA
  N2: Part1.A5/SCL, Part2.SCL, Part3.SCL
  VIN: Part1.3V3, Part2.VIN, Part3.VIN
  GND: Part1.GND, Part2.GND, Part3.GND

custom parts:
  Adafruit VL6180X Time of Flight Distance Sensor: The VL6180X is a Time of Flight distance sensor like no other you've used! The sensor contains a very tiny invisible laser source, and a matching sensor. The VL6180X can detect the "time of flight", or how long the light has taken to bounce back to the sensor. Since it uses a very narrow light source, it is good for determining distance of only the surface directly in front of it. Unlike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
