# Fritzing sketch ultrasonics only (saved by Fritzing 0.9.3b)
breadboards: 3

parts:
  Raspberry_Pi_1 = Raspberry Pi 3 [part_number=RPI-3-V1.2]
  Part1 = Adafruit T-Cobbler Plus [part_number="Adafruit #1989 and #2028"]
  hc-sr2 = hc-sr04
  R1 = Resistor [tolerance=±5% resistance=330 package=THT]
  R2 = Resistor [tolerance=±5% resistance=479 package=THT]
  hc-sr4 = hc-sr04
  R6 = Resistor [tolerance=±5% resistance=479 package=THT]
  R8 = Resistor [tolerance=±5% resistance=330 package=THT]

nets:
  3V3: Raspberry_Pi_1.3v3, Raspberry_Pi_1.3V3, Part1.+3.3V, Part1.+3.3V_2
  VCC: Raspberry_Pi_1.GPIO2, Part1.SDA, hc-sr2.VCC, hc-sr4.VCC
  N1: Raspberry_Pi_1.GPIO3, Part1.SCL
  N2: Raspberry_Pi_1.GIPO4, Part1.GPIO4
  GND: Raspberry_Pi_1.GND, Part1.GND, hc-sr2.Trig
  GND_2: Raspberry_Pi_1.GIPO17, Part1.GPIO17, hc-sr2.GND, R2.Pin_0, hc-sr4.GND, R6.Pin_0
  N3: Raspberry_Pi_1.GIPO27, Part1.GPIO27, R1.Pin_0, R2.Pin_1
  N4: Raspberry_Pi_1.GIPO22, Part1.GPIO22
  N5: Raspberry_Pi_1.GIPO10, Part1.MOSI
  N6: Raspberry_Pi_1.GIPO9, Part1.MISO
  N7: Raspberry_Pi_1.GIPO11, Part1.SCLK
  N8: Raspberry_Pi_1.ID_SD, Part1.EEDAT
  N9: Raspberry_Pi_1.GIPO5, Part1.GPIO5
  N10: Raspberry_Pi_1.GIPO6, Part1.GPIO6, hc-sr4.Trig
  N11: Raspberry_Pi_1.GIPO13, Part1.GPIO13, R6.Pin_1, R8.Pin_0
  N12: Raspberry_Pi_1.GIPO19, Part1.GPIO19
  N13: Raspberry_Pi_1.GIPO26, Part1.GPIO26
  N14: Raspberry_Pi_1.GIPO21, Part1.GPIO21
  N15: Raspberry_Pi_1.GIPO20, Part1.GPIO20
  N16: Raspberry_Pi_1.GIPO16, Part1.GPIO16
  N17: Raspberry_Pi_1.GIPO12, Part1.GPIO12
  N18: Raspberry_Pi_1.ID_SC, Part1.EECLK
  N19: Raspberry_Pi_1.GIPO7, Part1.CE1
  N20: Raspberry_Pi_1.GIPO8, Part1.CE0
  N21: Raspberry_Pi_1.GIPO25, Part1.GPIO25
  N22: Raspberry_Pi_1.GIPO24, Part1.GPIO24
  N23: Raspberry_Pi_1.GIPO23, Part1.GPIO23
  N24: Raspberry_Pi_1.GIPO18, Part1.GPIO18
  N25: Raspberry_Pi_1.GIPO15, Part1.RXD
  N26: Raspberry_Pi_1.GIPO14, Part1.TXD
  5V: Raspberry_Pi_1.5V, Part1.+5V
  N27: hc-sr2.Echo, R1.Pin_1
  N28: hc-sr4.Echo, R8.Pin_1

custom parts:
  Adafruit T-Cobbler Plus: The Raspberry Pi has landed on the Maker World like a 40-GPIO pinned, quad-USB ported, credit card sized bomb of DIY joy. And while you can use most of our great Model B accessories by hooking up our downgrade cable, its probably a good time to upgrade your set up and accessorize using all of the 40 pins. That's why we now carry the Assembled Adafruit Pi T-Cobbler Plus - Breakout + Cable for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
